// Logisim project 02 - Adders.circ as structural Verilog: 1 circuit, main circuit main
module main (
  input  A0,
  input  Carry_In,
  input  B0,
  input  A0_2,
  input  B0_2,
  input  A0_3,
  input  A1,
  input  B0_3,
  input  B1,
  input  Carry_In_2,
  input  A2,
  input  B2,
  input  A3,
  input  B3,
  input  Carry_In_3,
  input  [7:0] A_Inputs,
  input  [7:0] B_Inputs,
  output Carry_Out,
  output S0,
  output Sum_Out,
  output Sum_Out_2,
  output S1,
  output S2,
  output Carry_Out_2,
  output S3,
  output Carry_Out_3,
  output [7:0] Outputs,
  output Carry_Out_4
);

  wire adder_1_cout, adder_2_cout, adder_3_cout, and_1_out, and_2_out, xor_1_out;

  Adder #(.width(1)) adder_1 (.a(A0_2), .b(B0_2), .out(S0), .cin(Carry_In), .cout(adder_1_cout));
  Adder #(.width(1)) adder_2 (.a(A1), .b(B1), .out(S1), .cin(adder_1_cout), .cout(adder_2_cout));
  Adder #(.width(1)) adder_3 (.a(A2), .b(B2), .out(S2), .cin(adder_2_cout), .cout(adder_3_cout));
  Adder #(.width(1)) adder_4 (.a(A3), .b(B3), .out(S3), .cin(adder_3_cout), .cout(Carry_Out_3));
  xor xor_1 (xor_1_out, A0_3, B0_3);
  Adder adder_5 (.a(A_Inputs), .b(B_Inputs), .out(Outputs), .cin(Carry_In_3), .cout(Carry_Out_4));
  and and_1 (and_1_out, Carry_In_2, xor_1_out);
  and and_2 (and_2_out, A0_3, B0_3);
  xor xor_2 (Sum_Out_2, xor_1_out, Carry_In_2);
  or or_1 (Carry_Out_2, and_1_out, and_2_out);
  and and_3 (Carry_Out, A0, B0);
  xor xor_3 (Sum_Out, A0, B0);
endmodule
