// Logisim project 03 - Arith functions.circ as structural Verilog: 1 circuit, main circuit main
module main (
  input  [7:0] in_1,
  input  [7:0] in_2,
  input  [7:0] in_3,
  input  [7:0] in_4,
  input  [7:0] in_5,
  input  [7:0] in_6,
  input  [7:0] in_7,
  input  [7:0] in_8,
  input  [7:0] in_9,
  input  [7:0] in_10,
  output [7:0] out_11,
  output [7:0] out_12,
  output [7:0] out_13,
  output [7:0] out_14,
  output out_15,
  output out_16,
  output out_17
);

  Adder adder_1 (.a(in_1), .b(in_2), .out(out_11));  // open: cin, cout
  Subtractor subtractor_1 (.a(in_3), .b(in_4), .out(out_12));  // open: bin, bout
  Multiplier multiplier_1 (.a(in_5), .b(in_6), .out(out_13));  // open: cin, cout
  Divider divider_1 (.a(in_7), .b(in_8), .out(out_14));  // open: upper, rem
  Comparator comparator_1 (.a(in_9), .b(in_10), .gt(out_15), .eq(out_16), .lt(out_17));
  Hex_Digit_Display hex_digit_display_1 (.value(out_11[7:4]));  // open: dp
  Hex_Digit_Display hex_digit_display_2 (.value(out_11[3:0]));  // open: dp
endmodule
