// Logisim project 04 - Basic Memory.circ as structural Verilog: 1 circuit, main circuit main
module main (
  input  Reset,
  input  Set,
  input  Clock,
  input  Clock_2,
  input  Input,
  input  Toggle_Y_N,
  output Q,
  output Qbar,
  output Output,
  output Output_2
);

  D_Flip_Flop d_ff_1 (.clk(Clock), .D(Input), .Q(Output));  // open: Qn, preset, en, reset
  nand nand_1 (Q, Reset, Qbar);
  nand nand_2 (Qbar, Q, Set);
  T_Flip_Flop t_ff_1 (.clk(Clock_2), .T(Toggle_Y_N), .Q(Output_2));  // open: Qn, preset, reset, en

  // Notes on the sheet:
  //   D Flip-Flop
  //   S-R Flip Flip
  //   Toggle Flip-Flop
endmodule
