// Logisim project 05 - Registers.circ as structural Verilog: 1 circuit, main circuit main
module main (
  input  in_1,
  input  in_2,
  output out_3,
  output out_4,
  output out_5,
  output out_6,
  output out_7,
  output out_8,
  output out_9,
  output out_10
);

  wire clock_1_out, clock_2_out, t_ff_1_qn, t_ff_2_qn, t_ff_3_qn, t_ff_4_qn, t_ff_5_qn, t_ff_6_qn, t_ff_7_qn;

  Clock clock_1 (.out(clock_1_out));
  Clock clock_2 (.out(clock_2_out));
  D_Flip_Flop d_ff_1 (.clk(clock_1_out), .D(in_1), .Q(out_3));  // open: Qn, preset, en, reset
  T_Flip_Flop t_ff_1 (.clk(clock_2_out), .T(in_2), .Qn(t_ff_1_qn));  // open: Q, preset, reset, en
  D_Flip_Flop d_ff_2 (.clk(clock_1_out), .D(out_3), .Q(out_4));  // open: Qn, preset, en, reset
  T_Flip_Flop t_ff_2 (.clk(t_ff_1_qn), .T(in_2), .Qn(t_ff_2_qn));  // open: Q, preset, reset, en
  D_Flip_Flop d_ff_3 (.clk(clock_1_out), .D(out_4), .Q(out_5));  // open: Qn, preset, en, reset
  T_Flip_Flop t_ff_3 (.clk(t_ff_2_qn), .T(in_2), .Qn(t_ff_3_qn));  // open: Q, preset, reset, en
  D_Flip_Flop d_ff_4 (.clk(clock_1_out), .D(out_5), .Q(out_6));  // open: Qn, preset, en, reset
  T_Flip_Flop t_ff_4 (.clk(t_ff_3_qn), .T(in_2), .Qn(t_ff_4_qn));  // open: Q, preset, reset, en
  D_Flip_Flop d_ff_5 (.clk(clock_1_out), .D(out_6), .Q(out_7));  // open: Qn, preset, en, reset
  T_Flip_Flop t_ff_5 (.clk(t_ff_4_qn), .T(in_2), .Qn(t_ff_5_qn));  // open: Q, preset, reset, en
  D_Flip_Flop d_ff_6 (.clk(clock_1_out), .D(out_7), .Q(out_8));  // open: Qn, preset, en, reset
  T_Flip_Flop t_ff_6 (.clk(t_ff_5_qn), .T(in_2), .Qn(t_ff_6_qn));  // open: Q, preset, reset, en
  D_Flip_Flop d_ff_7 (.clk(clock_1_out), .D(out_8), .Q(out_9));  // open: Qn, preset, en, reset
  T_Flip_Flop t_ff_7 (.clk(t_ff_6_qn), .T(in_2), .Qn(t_ff_7_qn));  // open: Q, preset, reset, en
  D_Flip_Flop d_ff_8 (.clk(clock_1_out), .D(out_9), .Q(out_10));  // open: Qn, preset, en, reset
  T_Flip_Flop t_ff_8 (.clk(t_ff_7_qn), .T(in_2));  // open: Q, Qn, preset, reset, en
endmodule
