// Logisim project 06 - multiplexers and decoders.circ as structural Verilog: 1 circuit, main circuit main
module main (
  input  in_1,
  input  in_2,
  input  in_3,
  input  in_4,
  input  in_5,
  input  in_6,
  input  in_7,
  output out_8,
  output out_9,
  output out_10,
  output out_11,
  output out_12,
  output out_13,
  output out_14,
  output out_15,
  output out_16
);

  wire and_5_out, and_6_out, clock_1_out, not_1_out, not_2_out, not_3_out, not_4_out, not_5_out;

  Clock clock_1 (.out(clock_1_out));
  not not_1 (not_1_out, in_1);
  not not_2 (not_2_out, in_3);
  and and_1 (out_8, not_1_out, clock_1_out, not_2_out);
  and and_2 (out_10, in_1, clock_1_out, not_2_out);
  and and_3 (out_12, not_1_out, clock_1_out, in_3);
  and and_4 (out_14, in_1, clock_1_out, in_3);
  not not_3 (not_3_out, in_7);
  and and_5 (and_5_out, in_5, not_3_out);
  and and_6 (and_6_out, in_6, in_7);
  not not_4 (not_4_out, in_2);
  not not_5 (not_5_out, in_4);
  or or_1 (out_16, and_5_out, and_6_out);
  and and_7 (out_9, not_4_out, not_5_out);
  and and_8 (out_11, in_2, not_5_out);
  and and_9 (out_13, not_4_out, in_4);
  and and_10 (out_15, in_2, in_4);

  // Notes on the sheet:
  //   2 bit demultiplexer
  //   2 to 1 multiplexer
  //   2 bit decoder
endmodule
