// Logisim project 07 - displays.circ as structural Verilog: 1 circuit, main circuit main
module main (
  input  [3:0] in_1,
  input  in_2,
  input  in_3,
  input  [3:0] in_4,
  input  in_5
);

  wire clock_1_out;
  wire [3:0] counter_1_q, counter_1_q_2;
  wire [7:0] counter_2_q, rom_1_data, rom_2_data;

  Counter counter_1 (.Q({counter_1_q_2, counter_1_q}));  // open: load, D, count, carry, clk, clr
  Hex_Digit_Display hex_digit_display_1 (.value(counter_1_q_2));  // open: dp
  Hex_Digit_Display hex_digit_display_2 (.value(counter_1_q));  // open: dp
  Clock clock_1 (.out(clock_1_out));
  Counter counter_2 (.Q(counter_2_q), .clk(clock_1_out), .clr(in_3));  // open: load, D, count, carry
  ROM rom_1 (.addr({in_1, counter_2_q[3:0]}), .data(rom_1_data), .sel(in_2));
  ROM rom_2 (.addr({in_4, counter_2_q[7:4]}), .data(rom_2_data), .sel(in_5));
  _7_Segment_Display u_7_segment_display_1 (
    .g(rom_1_data[6]), .f(rom_1_data[5]), .a(rom_1_data[0]), .b(rom_1_data[1]), .e(rom_1_data[4]),
    .d(rom_1_data[3]), .c(rom_1_data[2]));  // open: dp
  _7_Segment_Display u_7_segment_display_2 (
    .g(rom_2_data[6]), .f(rom_2_data[5]), .a(rom_2_data[0]), .b(rom_2_data[1]), .e(rom_2_data[4]),
    .d(rom_2_data[3]), .c(rom_2_data[2]));  // open: dp

  // Notes on the sheet:
  //   http://forum.hosteng.com/wndm/HTMLHelp1/Instruction_Set/SEG_Hex_BCD_to_7_Segment_Display.htm
  //   contents of rom_1 (hex, n*v repeats v):
  //   3f 6 5b 4f 66 6d 7d 7 7f 67 77 7c 39 5e 79 71
  //   contents of rom_2 (hex, n*v repeats v):
  //   3f 6 5b 4f 66 6d 7d 7 7f 67 77 7c 39 5e 79 71
endmodule
