// Logisim project 08 - Boolen Algebra.circ as structural Verilog: 1 circuit, main circuit main
module main (
  input  X,
  input  in_2,
  input  X_2,
  input  in_4,
  input  X_3,
  input  in_6,
  input  X_4,
  input  in_8,
  input  in_9,
  input  in_10,
  input  in_11,
  input  in_12,
  input  in_13,
  input  in_14,
  input  in_15,
  input  in_16,
  input  in_17,
  input  in_18,
  input  in_19,
  input  in_20,
  input  in_21,
  input  in_22,
  output out_23,
  output out_24,
  output out_25,
  output out_26,
  output out_27,
  output out_28,
  output out_29,
  output out_30,
  output out_31,
  output out_32,
  output out_33,
  output out_34
);

  wire and_1_out, not_1_out, not_2_out, not_3_out, or_1_out, or_2_out;

  not not_1 (not_1_out, in_11);
  not not_2 (not_2_out, in_12);
  not not_3 (not_3_out, in_13);
  and and_1 (and_1_out, in_14, in_15);
  or or_1 (or_1_out, in_17, in_18);
  or or_2 (or_2_out, in_20, in_21);
  or or_3 (out_23, X, in_2);
  and and_2 (out_24, X_2, in_4);
  or or_4 (out_25, X_3, in_6);
  and and_3 (out_26, X_4, in_8);
  or or_5 (out_27, in_9, in_9);
  and and_4 (out_28, in_10, in_10);
  or or_6 (out_29, in_11, not_1_out);
  and and_5 (out_30, in_12, not_2_out);
  not not_4 (out_31, not_3_out);
  and and_6 (out_32, and_1_out, in_16);
  or or_7 (out_33, or_1_out, in_19);
  and and_7 (out_34, or_2_out, in_22);
endmodule
